// Digital circuit _sign_Extension.dig as structural Verilog
module sign_Extension (
  input  [24:0] Input,
  input  [1:0] ImmSrc,
  output [31:0] ImmExt
);

  wire [31:0] bitextender_1_out, bitextender_2_out, bitextender_3_out, bitextender_4_out;

  BitExtender #(.inputBits(12), .outputBits(32)) bitextender_1 (.in(Input[24:13]), .out(bitextender_1_out));
  BitExtender #(.inputBits(12), .outputBits(32)) bitextender_2 (
    .in({Input[24:18], Input[4:0]}), .out(bitextender_2_out));
  BitExtender #(.inputBits(13), .outputBits(32)) bitextender_3 (
    .in({Input[24], Input[0], Input[23:18], Input[4:1], 1'b0}), .out(bitextender_3_out));
  BitExtender #(.inputBits(21), .outputBits(32)) bitextender_4 (
    .in({Input[24], Input[12:5], Input[13], Input[23:14], 1'b0}), .out(bitextender_4_out));
  Multiplexer #(.Selector_Bits(2), .Bits(32)) multiplexer_1 (
    .sel(ImmSrc), .in_0(bitextender_1_out), .in_1(bitextender_2_out), .in_2(bitextender_3_out),
    .in_3(bitextender_4_out), .out(ImmExt));

  // Notes on the sheet:
  //   I - Type
  //   S-Type
  //   B - Type
  //   J - Type
endmodule
